# Fritzing sketch Circuit_Door_Monitor (saved by Fritzing 0.9.3b)
breadboards: 2

parts:
  S1 = Pushbutton [package="[THT]"]
  S2 = Pushbutton [package="[THT]"]
  R1 = Resistor [tolerance=±5% resistance=220 package=THT]
  R2 = Resistor [tolerance=±5% resistance=220 package=THT]
  LED1 = LED - 5mm [color="Red (633nm)" package="5 mm [THT]"]
  R5 = Resistor [tolerance=±5% resistance=220 package=THT]
  LCD1 = LCD screen
  U1 = PCF8574 [package="DIP16 [THT]"]
  Part2 = Arduino Mega 2560 (Rev3)
  KY-1 = Keyes Relay [package=THT]
  RHT1 = Humidity and Temperature Sensor RHT03

nets:
  GND: S1.Pin_1, S1.Pin_2, S2.Pin_1, S2.Pin_2, LED1.cathode, U1.GND, Part2.GND, KY-1.ground, RHT1.GND_2
  N1: S1.Pin_3, S1.Pin_4, R1.Pin_1, Part2.D22
  N2: S2.Pin_3, S2.Pin_4, R2.Pin_1, Part2.D24
  VCC: R1.Pin_0, R2.Pin_0, U1.A0, U1.A1, U1.A3, U1.VCC, Part2.5V, KY-1.power, RHT1.Vcc
  N3: LED1.anode, R5.Pin_0
  N4: R5.Pin_1, Part2.D28
  N5: LCD1.RS, U1.P0
  N6: LCD1.R/W, U1.P1
  N7: LCD1.E, U1.P2
  N8: LCD1.DB2, U1.P4
  N9: LCD1.DB3, U1.P5
  N10: LCD1.DB4, U1.P6
  N11: LCD1.DB5, U1.P7
  N12: U1.SCL, Part2.D21/SCL
  N13: U1.SDA, Part2.D20/SDA
  N14: Part2.D26, KY-1.signal
  N15: Part2.D30, RHT1.Data-signal

custom parts:
  Keyes Relay: The Keyes 5V relay module is suitable for SCM development, home appliance control. It uses a 5V~12V TIL control signal which can control DC / AC signal.
